# Fritzing sketch RetroStore (saved by Fritzing 0.9.3b)
circuit board: 9cm x 8cm
breadboards: 2

parts:
  IC2 = IC, DIP package, 20 pins [chip_label=74LVC245]
  IC1 = IC, DIP package, 20 pins [chip_label=ATF16V8B]
  J1 = double row female pin header, 50 pins [form="♀ (female)"]
  FET1 = 2N7000 FET N-Channel [part_number=2N7000 package=TO92]
  FET2 = 2N7000 FET N-Channel [part_number=2N7000 package=TO92]
  IC3 = IC, DIP package, 20 pins [chip_label=74LVC245]
  FET3 = 2N7000 FET N-Channel [part_number=2N7000 package=TO92]
  S1 = Pushbutton [package="[THT]"]
  LED1 = RGB LED (com. cathode, rgb) [package="5 mm [THT]"]
  ESP32 = ESP32S-HiLetgo [part_number=ESP32S-HiLetgo]

nets:
  N1: IC2.pin1, IC1.pin17, J1.pin17, IC3.pin2
  N2: IC2.pin2, J1.pin8
  N3: IC2.pin3, J1.pin7
  N4: IC2.pin4, J1.pin6
  N5: IC2.pin5, J1.pin5
  N6: IC2.pin6, J1.pin4
  N7: IC2.pin7, J1.pin3
  N8: IC2.pin8, J1.pin2
  N9: IC2.pin9, J1.pin1
  N10: IC2.pin10, IC1.pin10, J1.pin26, J1.pin27, J1.pin28, J1.pin29, J1.pin30, J1.pin31, J1.pin32, J1.pin33, J1.pin34, J1.pin35, J1.pin36, J1.pin37, J1.pin38, J1.pin39, J1.pin40, J1.pin41, J1.pin42, J1.pin43, J1.pin44, J1.pin45, J1.pin46, J1.pin47, J1.pin48, J1.pin49, J1.pin50, FET1.source, FET2.source, IC3.pin10, IC3.pin19, FET3.source, S1.Pin_3, S1.Pin_4, LED1.common_cathode, ESP32.GND
  N11: IC2.pin11, ESP32.GPIO12
  N12: IC2.pin12, ESP32.GPIO13
  N13: IC2.pin13, ESP32.GPIO14
  N14: IC2.pin14, ESP32.GPIO15
  N15: IC2.pin15, ESP32.GPIO16
  N16: IC2.pin16, ESP32.GPIO17
  N17: IC2.pin17, ESP32.GPIO18
  N18: IC2.pin18, ESP32.GPIO19
  N19: IC2.pin19, IC1.pin13, IC3.pin3
  N20: IC2.pin20, IC3.pin1, IC3.pin20, ESP32.3.3
  N21: IC1.pin2, J1.pin16
  N22: IC1.pin3, J1.pin15
  N23: IC1.pin4, J1.pin14
  N24: IC1.pin5, J1.pin13
  N25: IC1.pin6, J1.pin12
  N26: IC1.pin7, J1.pin11
  N27: IC1.pin8, J1.pin10
  N28: IC1.pin9, J1.pin9
  N29: IC1.pin12, ESP32.GPIO27
  N30: IC1.pin14, FET2.gate
  N31: IC1.pin15, FET1.gate
  N32: IC1.pin18, J1.pin18
  N33: IC1.pin19, J1.pin25
  N34: IC1.pin20, ESP32.VIN
  N35: J1.pin20, FET3.drain
  N36: J1.pin21, FET1.drain
  N37: J1.pin22, FET2.drain
  N38: IC3.pin17, ESP32.GPIO23
  N39: IC3.pin18, ESP32.GPIO36
  N40: FET3.gate, ESP32.GPIO25
  N41: S1.Pin_1, S1.Pin_2, ESP32.GPIO22
  N42: LED1.red_anode, ESP32.GPIO4
  N43: LED1.green_anode, ESP32.GPIO0
  N44: LED1.blue_anode, ESP32.GPIO21

notes:
  RetroStoreCard v1.1
  74LVC245
  ATF16V8B
  _
  B G - R
  2N7000
  ----------------------------------- GND -----------------------------------
  IOREQ*
  * = Active Low
  M1*
  NC
  IOWAIT*
  OUT*
  A7 A6 A5 A4 A3 A2 A1 A0 D7 D6 D5 D4 D3 D2 D1 D0
  49 47 45 43 41 39 37 35 33 31 29 27 25 23 21 19 17 15 13 11  9  7  5  3  1
  50 48 46 44 42 40 38 36 34 32 30 28 26 24 22 20 18 16 14 12 10  8  6  4  2
  EXTIOSEL*
  IN*
  RESET*
  IOINT*

custom parts:
  2N7000 FET N-Channel: A 2N7000 MOSFET N-Channel Transistor
  ESP32S-HiLetgo: HiLetgo ESP-WROOM-32 ESP32 ESP-32S Development Board 2.4GHz Dual-Mode WiFi + Bluetooth Dual Cores Microcontroller The ESP32 integrated with Antenna switches, RF Balun, power amplifiers, low-noise amplifiers, filters, and management modules, and the entire solution occupies the least area of PCB. 2.4 GHz Wi-Fi plus Bluetooth dual-mode chip, with TSMC Ultra-low power consumption 40nm technology,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
